# Fritzing sketch projet-arrosage-GI2S2 (saved by Fritzing 0.9.3b)
breadboards: 1

parts:
  Raspberry_Pi_2 = Raspberry Pi 3 [part_number=RPI-3-V1.2]
  Composant1 = Soil Moisture Sensor
  DHT1 = DHT11 Humitidy and Temperature Sensor
  KY-1 = Keyes Relay [package=THT]
  VALVE1 = Plastic Solenoid Valve
  Composant2 = Adafruit BMP280 [part_number="Adafruit #2651"]
  Composant4 = FC-28 Soil Hygrometer Module
  Power_plug1 = Power plug
  Composant5 = Adafruit PCF8591 [part_number="Adafruit #4648"]

nets:
  VCC: Raspberry_Pi_2.3v3, DHT1.VDD, Composant2.VCC, Composant4.VCC, Composant5.VCC
  N1: Raspberry_Pi_2.GPIO2, Composant5.SDA
  N2: Raspberry_Pi_2.GPIO3, Composant2.SCK/SCL, Composant5.SCL
  GND: Raspberry_Pi_2.GND, KY-1.ground, Composant5.GND
  N3: Raspberry_Pi_2.GPIO12, KY-1.signal
  N4: Raspberry_Pi_2.5V, KY-1.power
  N5: Composant1.GND, Composant4.NEG
  N6: DHT1.NULL, DHT1.GND
  N7: KY-1.C, VALVE1.no_name_yet#2
  N8: KY-1.NO, Power_plug1.VCC
  N9: Composant4.AO, Composant5.AIN1

custom parts:
  DHT11 Humitidy and Temperature Sensor: DHT11 Humidity and Temperature Sensor
  Keyes Relay: The Keyes 5V relay module is suitable for SCM development, home appliance control. It uses a 5V~12V TIL control signal which can control DC / AC signal.
  Adafruit BMP280: Bosch has stepped up their game with their new BMP280 sensor, an environmental sensor with temperature, barometric pressure that is the next generation upgrade to the BMP085/BMP180/BMP183. This sensor is great for all sorts of weather sensing and can even be used in both I2C and SPI! This precision sensor from Bosch is the best low-cost, precision sensing solution for measuring barometric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
  FC-28 Soil Hygrometer Module: The FC-28 is a soil hygrometer module that uses the Texas Instruments LM393 comparator chip to provide an analog measurement of soil humidity. The digital output is high when soil moisture is over a certain threshold, as determined by adjusting the potentiometer.
  Adafruit PCF8591: Measuring voltage and adjusting it is what electronics is all about so you won’t get far without friends like the PCF8591 ADC+DAC combo. Analog to Digital Converters help by measuring an analog voltage and turning it into something a microcontroller like a Metro or Arduino can understand. If you’re using a single board computer like a Raspberry Pi, you might not have any other way to measure a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
